# Fritzing sketch wiring (saved by Fritzing 0.9.2b)
circuit board: 8.46667cm x 5.64444cm
breadboards: 1

parts:
  DS18B20 = DS18B20 1-Wire Temperature Sensor Probe Cable  # not connected
  Raspberry_Pi_1 = Raspberry Pi 3
  Error_LED = LED - 5mm [color="Red (633nm)" package="5 mm [THT]"]
  Success_LED = LED - 5mm [color="Green (560nm)" package="5 mm [THT]"]
  DHT11 = DHT11 Humitidy and Temperature Sensor
  DS18B20_Resistor = Resistor [tolerance=±5% resistance=220 package="2512 [SMD]"]
  Error_LED_Resistor = Resistor [tolerance=±5% resistance=220 package="1206 [SMD]"]
  Success_LED_Resistor = Resistor [tolerance=±5% resistance=220 package="1206 [SMD]"]

nets (from the schematic view):
  N1: Raspberry_Pi_1.GIPO4, DS18B20_Resistor.Pin_0
  GND: Raspberry_Pi_1.GND, DHT11.GND, Error_LED_Resistor.Pin_0, Success_LED_Resistor.Pin_0
  N2: Raspberry_Pi_1.GIPO21, Error_LED.anode
  N3: Raspberry_Pi_1.GIPO20, Success_LED.anode
  N4: Raspberry_Pi_1.GIPO24, DHT11.DATA
  5V: Raspberry_Pi_1.5V, DHT11.VDD, DS18B20_Resistor.Pin_1
  N5: Error_LED.cathode, Error_LED_Resistor.Pin_1
  N6: Success_LED.cathode, Success_LED_Resistor.Pin_1

custom parts:
  DHT11 Humitidy and Temperature Sensor: DHT11 Humidity and Temperature Sensor
